# Fritzing sketch schematic (saved by Fritzing 0.9.2b)

parts:
  LCD1 = LCD screen
  Raspberry_Pi1 = Raspberry Pi 2
  R1 = Resistor [tolerance=±5% resistance=4.7k package=THT]
  R2 = Rotary Potentiometer (Small) [maximum_resistance=100kΩ package=THT]
  R3 = Resistor [tolerance=±5% resistance=470 package=THT]
  R4 = Resistor [tolerance=±5% resistance=470 package=THT]
  R5 = Resistor [tolerance=±5% resistance=470 package=THT]
  R6 = Resistor [tolerance=±5% resistance=470 package=THT]
  R7 = Resistor [tolerance=±5% resistance=470 package=THT]
  R8 = Resistor [tolerance=±5% resistance=470 package=THT]
  Q1 = NPN-Transistor [package="TO92 [THT]"]
  Q2 = LTR-301 [package=ltr-301]
  D1 = LTE-302 [package=lte-302]
  R9 = Resistor [tolerance=±5% resistance=330 package=THT]
  R10 = Resistor [tolerance=±5% resistance=4.7k package=THT]

nets:
  GND: LCD1.VSS, LCD1.R/W, Raspberry_Pi1.GND, R2.leg1, Q1.E, Q2.E
  VDD: LCD1.VDD, LCD1.LED+, Raspberry_Pi1.5V, R2.leg2
  N1: LCD1.V0, R2.wiper
  N2: LCD1.RS, R3.Pin_1
  N3: LCD1.E, R4.Pin_1
  N4: LCD1.DB4, R5.Pin_1
  N5: LCD1.DB5, R6.Pin_1
  N6: LCD1.DB6, R7.Pin_1
  N7: LCD1.DB7, R8.Pin_1
  N8: LCD1.LED-, Q1.C
  N9: Raspberry_Pi1.GPIO17, R6.Pin_0
  N10: Raspberry_Pi1.GPIO27, R7.Pin_0
  N11: Raspberry_Pi1.GPIO22, R8.Pin_0
  N12: Raspberry_Pi1.GPIO25, R3.Pin_0
  N13: Raspberry_Pi1.GPIO24, R4.Pin_0
  N14: Raspberry_Pi1.GPIO23, R5.Pin_0
  N15: Raspberry_Pi1.GPIO18, R1.Pin_0
  N16: Raspberry_Pi1.GPIO15, R9.Pin_0
  N17: Raspberry_Pi1.GPIO14, Q2.C, R10.Pin_1
  N18: R1.Pin_1, Q1.B
  N19: D1.A, R10.Pin_0
  N20: D1.C, R9.Pin_1
